# Fritzing sketch esquema (saved by Fritzing 0.9.3b)
breadboards: 1

parts:
  Controlador = Arduino Mega 2560 (Rev3)
  Servo_1_(SG90) = Basic Servo
  Servo_2_(SG90) = Basic Servo
  R1 = Resistor [tolerance=±5% resistance=10k package="0603 [SMD]"]
  LDR4 = Photocell (LDR) [package=THT]
  C1_(3300uf_6_3v) = Electrolytic Capacitor
  R2 = Resistor [tolerance=±5% resistance=10k package="0603 [SMD]"]
  LDR3 = Photocell (LDR) [package=THT]
  R3 = Resistor [tolerance=±5% resistance=10k package="0603 [SMD]"]
  LDR2 = Photocell (LDR) [package=THT]
  R4 = Resistor [tolerance=±5% resistance=10k package="0603 [SMD]"]
  LDR1 = Photocell (LDR) [package=THT]
  D1 = SOLAR-IXYS [package=solarbit-12x1]
  Componente1 = INA219 High Side DC Current Sensor Breakout [part_number=904]
  VCC1 = 4 x AAA Battery Mount
  R5 = Resistor [tolerance=±5% resistance=680 package="0805 [SMD]"]
  R6 = Resistor [tolerance=±5% resistance=680 package="0805 [SMD]"]
  R7 = Resistor [tolerance=±5% resistance=680 package="0805 [SMD]"]
  R8 = Resistor [tolerance=±5% resistance=330 package="0805 [SMD]"]
  R9 = Resistor [tolerance=±5% resistance=330 package="0805 [SMD]"]
  R10 = Resistor [tolerance=±5% resistance=330 package="0805 [SMD]"]
  Componente2 = MicroSD Card Module

nets:
  N1: Controlador.A0, R1.Pin_1, LDR4.pin_0
  N2: Controlador.A1, R2.Pin_1, LDR3.pin_0
  N3: Controlador.A2, R3.Pin_1, LDR2.pin_0
  N4: Controlador.A3, R4.Pin_1, LDR1.pin_0
  N5: Controlador.D21/SCL, Controlador.SCL, Componente1.SCL
  N6: Controlador.D20/SDA, Componente1.SDA
  N7: Controlador.D11_PWM, Servo_2_(SG90).pulse
  N8: Controlador.D9_PWM, Servo_1_(SG90).pulse
  VCC: Controlador.5V, Servo_1_(SG90).vcc, Servo_2_(SG90).vcc, LDR4.pin_1, C1_(3300uf_6_3v).+, LDR3.pin_1, LDR2.pin_1, LDR1.pin_1, Componente1.VCC, Componente2.VCC
  GND: Controlador.GND, Servo_1_(SG90).gnd, Servo_2_(SG90).gnd, R1.Pin_0, C1_(3300uf_6_3v).Capacitor_3300uf, R2.Pin_0, R3.Pin_0, R4.Pin_0, D1.C, Componente1.GND, VCC1.-, R5.Pin_0, R6.Pin_0, R7.Pin_0, Componente2.GND
  N9: Controlador.D4_PWM, Componente2.MISO
  N10: Controlador.D5_PWM, R10.Pin_1
  N11: Controlador.D6_PWM, R9.Pin_1
  N12: Controlador.D7_PWM, R8.Pin_1
  N13: D1.A, Componente1.VIN+
  N14: Componente1.VIN-, VCC1.+
  N15: R5.Pin_1, R8.Pin_0, Componente2.CS
  N16: R6.Pin_1, R9.Pin_0, Componente2.SCK
  N17: R7.Pin_1, R10.Pin_0, Componente2.MOSI

custom parts:
  Electrolytic Capacitor: 1000µF electrolytic capacitor
  INA219 High Side DC Current Sensor Breakout: This breakout board will solve all your power-monitoring problems. Instead of struggling with two multimeters, you can just use the handy INA219B chip on this breakout to both measure both the high side voltage and DC current draw over I2C with 1% precision. Most current-measuring devices such as our current panel meter are only good for low side measuring. That means that unless you want to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
